// Logisim project NAND2Tetris.circ as structural Verilog: 3 circuits, main circuit ALU
module main (
);

  ALU ALU ();  // open: x, y, zx, nx, zy, ny, f, no, out, zr, ng
endmodule

module ALU (
  input  [15:0] x,
  input  [15:0] y,
  input  zx,
  input  nx,
  input  zy,
  input  ny,
  input  f,
  input  no,
  output [15:0] out,
  output zr,
  output ng
);

  wire NO_t, NX_t, NY_t, ZX_t, ZY_t;
  wire [15:0] adder_1_out, and_1_out, and_2_out, and_3_out, multiplexer_1_out, multiplexer_2_out,
       multiplexer_3_out, multiplexer_4_out, multiplexer_5_out, not_6_out, not_7_out, not_8_out, not_9_out,
       not_10_out;

  not not_1 (ZX_t, zx);
  not not_2 (NX_t, nx);
  not not_3 (ZY_t, zy);
  not not_4 (NY_t, ny);
  not not_5 (NO_t, no);
  assign not_6_out = ~x;  // NOT_Gate not_6, 16 bits wide
  // Probe on not_6_out
  assign and_1_out = not_6_out & x;  // AND_Gate and_1, 16 bits wide
  // Probe on not_7_out
  assign not_7_out = ~y;  // NOT_Gate not_7, 16 bits wide
  assign and_2_out = not_7_out & y;  // AND_Gate and_2, 16 bits wide
  // Probe on and_1_out
  // Probe on multiplexer_1_out
  Multiplexer #(.width(16), .enable("false")) multiplexer_1 (
    .in0(and_1_out), .in1(x), .out(multiplexer_1_out), .sel(ZX_t));
  // Probe on and_2_out
  assign not_8_out = ~multiplexer_1_out;  // NOT_Gate not_8, 16 bits wide
  // Probe on multiplexer_2_out
  Multiplexer #(.width(16), .enable("false")) multiplexer_2 (
    .in0(and_2_out), .in1(y), .out(multiplexer_2_out), .sel(ZY_t));
  assign not_9_out = ~multiplexer_2_out;  // NOT_Gate not_9, 16 bits wide
  Multiplexer #(.width(16), .enable("false")) multiplexer_3 (
    .in0(not_8_out), .in1(multiplexer_1_out), .out(multiplexer_3_out), .sel(NX_t));
  Multiplexer #(.width(16), .enable("false")) multiplexer_4 (
    .in0(not_9_out), .in1(multiplexer_2_out), .out(multiplexer_4_out), .sel(NY_t));
  assign and_3_out = multiplexer_4_out & multiplexer_3_out;  // AND_Gate and_3, 16 bits wide
  Adder #(.width(16)) adder_1 (.a(multiplexer_4_out), .b(multiplexer_3_out), .out(adder_1_out));  // open: cin, cout
  Multiplexer #(.width(16), .enable("false")) multiplexer_5 (
    .in0(and_3_out), .in1(adder_1_out), .out(multiplexer_5_out), .sel(f));
  Comparator #(.width(16), .mode("unsigned")) comparator_1 (.a(out), .b({16{1'b0}}), .eq(zr));  // open: gt, lt
  BitSelector #(.width(16)) bitselector_1 (.in(out), .out(ng), .sel(4'b1000));
  assign not_10_out = ~multiplexer_5_out;  // NOT_Gate not_10, 16 bits wide
  Multiplexer #(.width(16), .enable("false")) multiplexer_6 (
    .in0(not_10_out), .in1(multiplexer_5_out), .out(out), .sel(NO_t));
endmodule

module CPU (
  input  [15:0] inM,
  input  [15:0] instruction
);
endmodule
